// Logisim project NOT_gate_assignment.circ as structural Verilog
module main (
  input  in_1,
  output out_2
);

  not_gate not_gate_1 (.a(in_1), .y(out_2));
endmodule

// VHDL entity not_gate, as the project stores it:
library ieee;
use ieee.std_logic_1164.all;

entity not_gate is
    port (
        a : in std_logic;
        y : out std_logic
    );
end entity not_gate;

architecture behavioral of not_gate is
begin
    y <= not a;
end architecture behavioral;
